# Fritzing sketch Arduino Invaders (saved by Fritzing 0.8.7b)
circuit board: 6.88566cm x 5.36311cm
breadboards: 3

parts:
  LCD1 = LCD screen
  Arduino1 = Arduino Uno (Rev3)
  R3 = Resistor [tolerance=±5% resistance=1.2 package=THT]
  S1 = Pushbutton [package="[THT]"]
  S2 = Pushbutton [package="[THT]"]
  R4 = Resistor [tolerance=±5% resistance=120k package=THT]
  R5 = Resistor [tolerance=±5% resistance=120k package=THT]
  S3 = Pushbutton [package="[THT]"]
  R6 = Resistor [tolerance=±5% resistance=120k package=THT]  # not connected
  R7 = Rotary Potentiometer (Small) [maximum_resistance=100kΩ package=THT]  # not connected

nets (from the schematic view):
  VSS: LCD1.VSS, LCD1.R/W, LCD1.LED-, Arduino1.GND, R3.Pin_0, R4.Pin_0, R5.Pin_0
  VDD: LCD1.VDD, Arduino1.5V, S1.Pin_1, S1.Pin_2, S2.Pin_1, S2.Pin_2
  N1: LCD1.V0, R3.Pin_1
  N2: LCD1.RS, Arduino1.D12/MISO
  N3: LCD1.E, Arduino1.D11_PWM/MOSI
  N4: LCD1.DB4, Arduino1.D5_PWM
  N5: LCD1.DB5, Arduino1.D4
  N6: LCD1.DB6, Arduino1.D3_PWM
  N7: LCD1.DB7, Arduino1.D2
  N8: Arduino1.A4/SDA, S1.Pin_3, S1.Pin_4, R5.Pin_1
  N9: Arduino1.A5/SCL, S2.Pin_3, S2.Pin_4, R4.Pin_1
  N10: S3.Pin_1, S3.Pin_2
  N11: S3.Pin_3, S3.Pin_4

notes:
  Standard 16 pin lcd connection will work with every size
  1.2k contrast resistor
  Without the backlight you get a bit of 'motion blur', with the backlight you can see everything blinking so I disconnected it
  Left and right button with pull-down risistor
  Potmeter and shoot button with pull down resistor
