# Fritzing sketch BareBoneArduinoInvaders (saved by Fritzing 0.9.3b)
circuit board: 8.46667cm x 5.64444cm
breadboards: 2

parts:
  U1 = atmega328 [package=dip]
  C2 = Capacitor [package=cap-pth-small2]
  C3 = Capacitor [package=cap-pth-small2]
  Y1 = CRYSTAL [package=crystal-smd-10.5x4.8-2pin]
  VCC1 = 4 x AAA Battery Mount
  R9 = Resistor [tolerance=±5% resistance=1.2 package=THT]
  S5 = Pushbutton [package="[THT]"]
  S6 = Pushbutton [package="[THT]"]
  R10 = Resistor [tolerance=±5% resistance=120k package=THT]
  R12 = Resistor [tolerance=±5% resistance=120k package=THT]
  LCD2 = LCD screen

nets:
  N1: U1.D2, LCD2.DB7
  N2: U1.D3_(PWM), LCD2.DB6
  N3: U1.D4, LCD2.DB5
  VCC: U1.VCC, U1.AVCC, U1.AREF, VCC1.+, S5.Pin_1, S5.Pin_2, S6.Pin_1, LCD2.VDD
  N4: U1.GND#7, C2.1, C3.2, VCC1.-
  N5: U1.XLAT1, C2.2, Y1.2
  N6: U1.XLAT2, C3.1, Y1.1
  N7: U1.D5_(PWM), LCD2.DB4
  N8: U1.D11_(PWM), LCD2.E
  N9: U1.D12, LCD2.RS
  N10: U1.GND#21, R9.Pin_0, R10.Pin_0, R12.Pin_0, LCD2.VSS, LCD2.R/W, LCD2.LED-
  N11: U1.A4, S6.Pin_3, S6.Pin_4, R10.Pin_1
  N12: U1.A5, S5.Pin_3, S5.Pin_4, R12.Pin_1
  N13: R9.Pin_1, LCD2.V0

notes:
  Capacitors: 22 pF
  Crystal: 16 MHz
  Standard 16 pin lcd connection will work with every size
  1.2k contrast resistor
  Without the backlight you get a bit of 'motion blur', with the backlight you can see everything blinking so I disconnected it
  Left and right button with pull-down risistor
